# Fritzing sketch Reader_for_Sensors_DIY (saved by Fritzing 0.9.3b)
circuit board: 7.00001cm x 2.80048cm
breadboards: 1

parts:
  Metro_Mini = Adafruit Metro Mini [part_number="Adafruit #2590"]
  100uF = Electrolytic Capacitor [capacitance=0.1mF voltage=25V package="0605 [SMD, electrolytic]"]
  Sensor = female pin header, 4 pins [form="♀ (female)"]
  ADS1115 = Adafruit ADS1115 16Bit I2C ADC [part_number="Adafruit #1085"]
  R1 = Resistor [tolerance=±5% resistance=10k package="1206 [SMD]"]
  100nF = Capacitor [package=1206]

nets:
  N1: Metro_Mini.AD5/SCL, ADS1115.SCL
  N2: Metro_Mini.AD4/SDA, ADS1115.SDA
  N3: Metro_Mini.IO6, Sensor.pin1, R1.Pin_0
  N4: Metro_Mini.IO2, Sensor.pin3
  +5V: Metro_Mini.+5V, 100uF.+, ADS1115.VDD, 100nF.2
  GND: Metro_Mini.GND, 100uF.-, Sensor.pin4, ADS1115.AIN1, ADS1115.GND, R1.Pin_1, 100nF.1
  N5: Sensor.pin2, ADS1115.AIN0

notes:
  V+
  WC
  T
  GND
  AVAN Zero
  DurUntash Lab
  San Diego, CA

custom parts:
  Adafruit Metro Mini: We sure love the ATmega328 here at Adafruit, and we use them a lot for our own projects. The processor has plenty of GPIO, Analog inputs, hardware UART SPI and I2C, timers and PWM galore - just enough for most simple projects. When we need to go small, we use a Pro Trinket 3V or 5V, but if you want to have USB-to-Serial built in, we reach for an Adafruit METRO Mini. METRO Mini is the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
  Adafruit ADS1115 16Bit I2C ADC: For microcontrollers without an analog-to-digital converter or when you want a higher-precision ADC, the ADS1115 provides 16-bit precision at 860 samples/second over I2C. The chip can be configured as 4 single-ended input channels, or two differential channels. As a nice bonus, it even includes a programmable gain amplifier, up to x16, to help boost up smaller single/differential signals to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
