# Fritzing sketch Reader_w_Display_for_Sensors_DIY (saved by Fritzing 0.9.3b)
circuit board: 7.174cm x 6.63946cm
breadboards: 2

parts:
  47uF = Electrolytic Capacitor [capacitance=47µF voltage=25V package="0605 [SMD, electrolytic]"]
  SW = female pin header, 2 pins [form="♀ (female)"]
  PB1 = Adafruit MiniBoost 5V 100mA Charge Pump AP3602A [part_number=3661]
  Sensor = female pin header, 4 pins [form="♀ (female)"]
  Res = female pin header, 2 pins [form="♀ (female)"]
  ADC = Adafruit ADS1115 16Bit I2C ADC [part_number="Adafruit #1085"]
  10K = Resistor [tolerance=±5% resistance=10k package="1206 [SMD]"]
  10K_2 = Resistor [tolerance=±5% resistance=10k package="1206 [SMD]"]
  100nF = Capacitor [package=1206]
  Micro = Adafruit Feather 32u4 Adalogger [part_number="Adafruit #2795"]
  100K = Resistor [tolerance=±5% resistance=100k package="1206 [SMD]"]
  100nF_2 = Capacitor [package=1206]
  100K_2 = Resistor [tolerance=±5% resistance=100k package="1206 [SMD]"]
  LED = female pin header, 2 pins [form="♀ (female)"]
  2K2 = Resistor [tolerance=±5% resistance=2.2k package="1206 [SMD]"]
  10K_3 = Resistor [tolerance=±5% resistance=10k package="1206 [SMD]"]
  OLED = female pin header, 4 pins [form="♀ (female)"]

nets:
  GND: 47uF.-, SW.pin2, PB1.GND, Sensor.pin4, Res.pin2, ADC.AIN1, ADC.ADDR, ADC.GND, 100nF.1, Micro.GND, 100K.Pin_0, 100nF_2.1, LED.pin2, 10K_3.Pin_0, OLED.pin1
  VIN: 47uF.+, PB1.VIN, ADC.VDD, 10K.Pin_0, 10K_2.Pin_0, 100nF.2, Micro.+3V3, OLED.pin2
  N1: SW.pin1, Micro.EN
  N2: PB1.!SHDN, Micro.A0
  N3: PB1.5.0V, Sensor.pin1, 10K_3.Pin_1
  N4: Sensor.pin2, ADC.AIN0
  N5: Sensor.pin3, Micro.12
  N6: Res.pin1, Micro.RST
  N7: ADC.SDA, 10K_2.Pin_1, Micro.2, OLED.pin4
  N8: ADC.SCL, 10K.Pin_1, Micro.3, OLED.pin3
  N9: Micro.A2, 100K.Pin_1, 100nF_2.2, 100K_2.Pin_0
  N10: Micro.VBUS, 100K_2.Pin_1
  N11: Micro.13, 2K2.Pin_0
  N12: LED.pin1, 2K2.Pin_1

notes:
  V+
  San Diego, CA
  DurUntash Lab
  AVAN Reader
  T
  WC
  GND
  SD
  SC

custom parts:
  Adafruit MiniBoost 5V 100mA Charge Pump AP3602A: This adorable little board will come in very handy whenever you need a small amount of 5V power. It's the size of a linear regulator, but it's actually a mini-booster! Input 3V on one side, and get 5V at up to 100mA supply on the other. Perfect for use with battery-powered projects with 2 or 3 Alkaline, or a single Lithium battery. This booster uses a charge-pump topology, which makes it very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
  Adafruit ADS1115 16Bit I2C ADC: For microcontrollers without an analog-to-digital converter or when you want a higher-precision ADC, the ADS1115 provides 16-bit precision at 860 samples/second over I2C. The chip can be configured as 4 single-ended input channels, or two differential channels. As a nice bonus, it even includes a programmable gain amplifier, up to x16, to help boost up smaller single/differential signals to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
  Adafruit Feather 32u4 Adalogger: This is the Adafruit Feather 32u4 Adalogger - our take on an 'all-in-one' datalogger (or data-reader) with built in USB and battery charging. Its an Adafruit Feather 32u4 with a microSD holder ready to rock! We have other boards in the Feather family, check'em out here At the Feather 32u4's heart is at ATmega32u4 clocked at 8 MHz and at 3.3V logic, a chip setup we've had tons of experience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
